# Fritzing sketch BITBA555_tutorial1 (saved by Fritzing 0.9.3b)
breadboards: 1

parts:
  Arduino_Uno = Arduino Uno (Rev3)
  MCP4921 = IC, DIP package, 8 pins [chip_label=IC]
  C1 = Ceramic Capacitor [capacitance=100nF package="100 mil [THT, multilayer]"]
  SharpPC817 = Sharp PC817 [package=THT]
  D1 = Rectifier Diode [part_number=1N4001 package="300 mil [THT]"]
  MIDI_IN = MIDI_CONN_FEMALE_SUPPORT [package=din_5_female_support]
  MIDI_OUT = MIDI_CONN_FEMALE_SUPPORT [package=din_5_female_support]
  R1 = Resistor [tolerance=±5% resistance=180 package=THT]
  R2 = Resistor [tolerance=±5% resistance=560 package=THT]
  R3 = Resistor [tolerance=±5% resistance=220 package=THT]
  R4 = Resistor [tolerance=±5% resistance=220 package=THT]

nets:
  N1: Arduino_Uno.D10_PWM/SS, MCP4921.pin2
  N2: Arduino_Uno.D11_PWM/MOSI, MCP4921.pin4
  N3: Arduino_Uno.D13/SCK, MCP4921.pin3
  N4: Arduino_Uno.D0/RX, SharpPC817.Pin_4, R2.Pin_0
  N5: Arduino_Uno.D1/TX, R4.Pin_1
  5V: Arduino_Uno.5V, MCP4921.pin1, MCP4921.pin6, C1.1, R2.Pin_1, R3.Pin_1
  GND: Arduino_Uno.GND, MCP4921.pin5, MCP4921.pin7, C1.0, SharpPC817.Pin_3
  N6: SharpPC817.Pin_1, D1.cathode, R1.Pin_1
  N7: SharpPC817.Pin_2, D1.anode, MIDI_IN.MIDI_OUT
  N8: MIDI_IN.MIDI_IN, R1.Pin_0
  N9: MIDI_OUT.MIDI_IN, R3.Pin_0
  N10: MIDI_OUT.MIDI_OUT, R4.Pin_0
