# Fritzing sketch BITBA555_tutorial3 (saved by Fritzing 0.9.3b)
breadboards: 1

parts:
  uA741 = IC, DIP package, 8 pins [chip_label=IC]
  R1 = Resistor [tolerance=±5% resistance=220k package=THT]
  R2 = Resistor [tolerance=±5% resistance=220k package=THT]
  uA741_2 = IC, DIP package, 8 pins [chip_label=IC]
  R3 = Resistor [tolerance=±5% resistance=180 package=THT]
  C1 = Ceramic Capacitor [capacitance=10pF package="100 mil [THT, multilayer]"]
  C2 = Electrolytic Capacitor [capacitance=10µF voltage=20V package="100 mil [THT, electrolytic]"]
  C3 = Electrolytic Capacitor [capacitance=100µF voltage=20V package="200 mil [THT, electrolytic]"]
  IC1 = OTA [package="DIP (Dual Inline) [THT]"]
  IC1_1 = OTA [package="DIP (Dual Inline) [THT]"]
  IC1_2 = OTA [package="DIP (Dual Inline) [THT]"]
  IC1_3 = OTA [package="DIP (Dual Inline) [THT]"]
  IC1_4 = OTA [package="DIP (Dual Inline) [THT]"]
  part = OTA [package="DIP (Dual Inline) [THT]"]
  R4 = Resistor [tolerance=±5% resistance=180 package=THT]
  R5 = Resistor [tolerance=±5% resistance=100k package=THT]
  R6 = Resistor [tolerance=±5% resistance=15k package=THT]
  R7 = Resistor [tolerance=±5% resistance=180 package=THT]
  R8 = Resistor [tolerance=±5% resistance=10k package=THT]
  R9 = Resistor [tolerance=±5% resistance=100k package=THT]
  R10 = Resistor [tolerance=±5% resistance=15k package=THT]
  R11 = Resistor [tolerance=±5% resistance=100k package=THT]
  R12 = Resistor [tolerance=±5% resistance=180 package=THT]
  R13 = Resistor [tolerance=±5% resistance=10k package=THT]
  R14 = Resistor [tolerance=±5% resistance=100k package=THT]
  C4 = Ceramic Capacitor [capacitance=300pF package="100 mil [THT, multilayer]"]
  R15 = Resistor [tolerance=±5% resistance=180 package=THT]
  C5 = Ceramic Capacitor [capacitance=300pF package="100 mil [THT, multilayer]"]
  part_2 = OTA [package="DIP (Dual Inline) [THT]"]
  IC2_4 = OTA [package="DIP (Dual Inline) [THT]"]
  IC2_1 = OTA [package="DIP (Dual Inline) [THT]"]
  IC2 = OTA [package="DIP (Dual Inline) [THT]"]
  IC2_3 = OTA [package="DIP (Dual Inline) [THT]"]
  IC2_2 = OTA [package="DIP (Dual Inline) [THT]"]
  R16 = Resistor [tolerance=±5% resistance=180 package=THT]
  R17 = Resistor [tolerance=±5% resistance=100k package=THT]
  R18 = Resistor [tolerance=±5% resistance=15k package=THT]
  R19 = Resistor [tolerance=±5% resistance=180 package=THT]
  R20 = Resistor [tolerance=±5% resistance=10k package=THT]
  R21 = Resistor [tolerance=±5% resistance=100k package=THT]
  R22 = Resistor [tolerance=±5% resistance=15k package=THT]
  R23 = Resistor [tolerance=±5% resistance=100k package=THT]
  R24 = Resistor [tolerance=±5% resistance=180 package=THT]
  R25 = Resistor [tolerance=±5% resistance=10k package=THT]
  R26 = Resistor [tolerance=±5% resistance=100k package=THT]
  C6 = Ceramic Capacitor [capacitance=300pF package="100 mil [THT, multilayer]"]
  R27 = Resistor [tolerance=±5% resistance=180 package=THT]
  C7 = Ceramic Capacitor [capacitance=300pF package="100 mil [THT, multilayer]"]
  R28 = Rotary Potentiometer (Small) [maximum_resistance=1MΩ package=THT]
  R29 = Resistor [tolerance=±5% resistance=50k package=THT]
  R30 = Rotary Potentiometer (Small) [maximum_resistance=1MΩ package=THT]
  R31 = Resistor [tolerance=±5% resistance=1k package=THT]
  uA741_3 = IC, DIP package, 8 pins [chip_label=IC]
  R32 = Rotary Potentiometer (Small) [maximum_resistance=100kΩ package=THT]
  C8 = Ceramic Capacitor [capacitance=100nF package="100 mil [THT, multilayer]"]
  C9 = Ceramic Capacitor [capacitance=100nF package="100 mil [THT, multilayer]"]
  C10 = Ceramic Capacitor [capacitance=100nF package="100 mil [THT, multilayer]"]

nets:
  VGND: uA741.pin2, uA741_2.pin2, uA741_2.pin6, C1.1, R4.Pin_1, R7.Pin_0, R12.Pin_1, C4.0, R15.Pin_0, R16.Pin_1, R19.Pin_0, R24.Pin_1, C6.0, R27.Pin_0
  N1: uA741.pin3, R1.Pin_0, R2.Pin_1
  GND: uA741.pin4, R2.Pin_0, uA741_2.pin4, C2.-, C3.-, IC1.connector5, part.pin6, R8.Pin_0, R13.Pin_0, part_2.pin6, IC2.connector5, R20.Pin_0, R25.Pin_0, uA741_3.pin4, R32.leg1, C8.0, C9.0, C10.0
  N2: uA741.pin6, R3.Pin_0, C1.0
  18V: uA741.pin7, R1.Pin_1, uA741_2.pin7, C2.+, C3.+, IC1.connector10, IC1_2.pin11, R6.Pin_0, R10.Pin_0, IC2.connector10, IC2_2.pin11, R18.Pin_0, R22.Pin_0, uA741_3.pin7, R32.leg2, C8.1, C9.1, C10.1
  N3: uA741_2.pin3, R3.Pin_1
  N4: IC1.connector0, IC1.connector15, IC1_1.pin1, IC1_3.pin16, IC2_1.pin1, IC2.connector0, IC2.connector15, IC2_3.pin16, R31.Pin_1
  N5: IC1.connector1, IC1_1.pin2, R6.Pin_1
  N6: IC1.connector2, IC1_1.pin3, R4.Pin_0, R5.Pin_1
  N7: IC1.connector3, IC1_1.pin4, R7.Pin_1, R9.Pin_0, R29.Pin_0
  N8: IC1.connector4, IC1.connector6, IC1_1.pin5, IC1_2.pin7, C5.1
  N9: IC1.connector7, IC1_2.pin8, R8.Pin_1, R9.Pin_1, R11.Pin_0
  N10: IC1.connector8, IC1_4.pin9, R13.Pin_1, R14.Pin_0, C5.0, R17.Pin_0
  N11: IC1.connector9, IC1.connector11, IC1_3.pin12, IC1_4.pin10, C4.1
  N12: IC1.connector12, IC1_3.pin13, R14.Pin_1, R15.Pin_1
  N13: IC1.connector13, IC1_3.pin14, R11.Pin_1, R12.Pin_0
  N14: IC1.connector14, IC1_3.pin15, R10.Pin_1
  audio_in: R5.Pin_0
  N15: IC2_4.pin9, IC2.connector8, R25.Pin_1, R26.Pin_0, C7.0, R28.leg1, R28.wiper
  N16: IC2_4.pin10, IC2.connector9, IC2.connector11, IC2_3.pin12, C6.1
  N17: IC2_1.pin2, IC2.connector1, R18.Pin_1
  N18: IC2_1.pin3, IC2.connector2, R16.Pin_0, R17.Pin_1
  N19: IC2_1.pin4, IC2.connector3, R19.Pin_1, R21.Pin_0
  N20: IC2_1.pin5, IC2.connector4, IC2.connector6, IC2_2.pin7, C7.1
  N21: IC2.connector7, IC2_2.pin8, R20.Pin_1, R21.Pin_1, R23.Pin_0
  N22: IC2.connector12, IC2_3.pin13, R26.Pin_1, R27.Pin_1
  N23: IC2.connector13, IC2_3.pin14, R23.Pin_1, R24.Pin_0
  N24: IC2.connector14, IC2_3.pin15, R22.Pin_1
  N25: R28.leg2, R29.Pin_1
  N26: R30.leg1, R30.wiper, R31.Pin_0
  CV: R30.leg2, uA741_3.pin2, uA741_3.pin6
  N27: uA741_3.pin3, R32.wiper

custom parts:
  OTA: Operational Transconductance Amplifier
  OTA: Operational Transconductance Amplifier
  OTA: Operational Transconductance Amplifier
  OTA: Operational Transconductance Amplifier
  OTA: Operational Transconductance Amplifier
  OTA: Operational Transconductance Amplifier
