# Fritzing sketch BITBA555_tutorial4 (saved by Fritzing 0.9.3b)
breadboards: 2

parts:
  Q1 = NPN-Transistor [package="TO92 [THT]"]
  Q2 = NPN-Transistor [package="TO92 [THT]"]
  Q3 = NPN-Transistor [package="TO92 [THT]"]
  R1 = Resistor [tolerance=±5% resistance=5.6k package=THT]
  R2 = Resistor [tolerance=±5% resistance=5.6k package=THT]
  R3 = Resistor [tolerance=±5% resistance=5.6k package=THT]
  R4 = Resistor [tolerance=±5% resistance=10k package=THT]
  R5 = Resistor [tolerance=±5% resistance=10k package=THT]
  R6 = Resistor [tolerance=±5% resistance=10k package=THT]
  C1 = Ceramic Capacitor [capacitance=100nF package="100 mil [THT, multilayer]"]
  D1 = Rectifier Diode [part_number=1N4148 package="300 mil [THT]"]
  D2 = Rectifier Diode [part_number=1N4148 package="300 mil [THT]"]
  R7 = Resistor [tolerance=±5% resistance=1k package=THT]
  U1 = 555 Timer [part_number=NE555 package="DIP8 [THT]"]
  C2 = Ceramic Capacitor [capacitance=100nF package="100 mil [THT, multilayer]"]
  C3 = Ceramic Capacitor [capacitance=100nF package="100 mil [THT, multilayer]"]
  D3 = Rectifier Diode [part_number=1N4148 package="300 mil [THT]"]
  R8 = Resistor [tolerance=±5% resistance=180 package=THT]
  Attack = Rotary Potentiometer (Small) [maximum_resistance=1M package=THT]
  C4 = Electrolytic Capacitor [capacitance=3.3µF package="100 mil [THT, electrolytic]"]
  D4 = Rectifier Diode [part_number=1N4148 package="300 mil [THT]"]
  R9 = Resistor [tolerance=±5% resistance=180 package=THT]
  Release = Rotary Potentiometer (Small) [maximum_resistance=500k package=THT]
  D5 = Rectifier Diode [part_number=1N4001 package="300 mil [THT]"]
  R10 = Resistor [tolerance=±5% resistance=180 package=THT]
  U2 = LM 358 Dual Op-Amp [part_number=LM358 package="DIP8 [THT]"]
  Decay = Rotary Potentiometer (Small) [maximum_resistance=500k package=THT]
  R11 = Resistor [tolerance=±5% resistance=5.6k package=THT]
  Sustain = Rotary Potentiometer (Small) [maximum_resistance=100kΩ package=THT]
  R12 = Resistor [tolerance=±5% resistance=8k package=THT]
  R13 = Resistor [tolerance=±5% resistance=10k package=THT]
  C5 = Ceramic Capacitor [capacitance=100nF package="100 mil [THT, multilayer]"]
  IC1 = IC, DIP package, 8 pins [chip_label=IC part_number=OP27]
  R14 = Resistor [tolerance=±5% resistance=10k package=THT]
  R15 = Resistor [tolerance=±5% resistance=10k package=THT]
  IC2 = OTA [package="DIP (Dual Inline) [THT]"]
  IC2_1 = OTA [package="DIP (Dual Inline) [THT]"]
  IC2_2 = OTA [package="DIP (Dual Inline) [THT]"]
  IC2_3 = OTA [package="DIP (Dual Inline) [THT]"]
  IC2_4 = OTA [package="DIP (Dual Inline) [THT]"]  # not connected
  Part1 = OTA [package="DIP (Dual Inline) [THT]"]
  R16 = Rotary Potentiometer (Small) [maximum_resistance=1k package=THT]
  R17 = Resistor [tolerance=±5% resistance=30k package=THT]
  C6 = Ceramic Capacitor [capacitance=100nF package="100 mil [THT, multilayer]"]
  R18 = Resistor [tolerance=±5% resistance=5.6k package=THT]
  R19 = Resistor [tolerance=±5% resistance=30k package=THT]
  C7 = Electrolytic Capacitor [capacitance=47µF package="100 mil [THT, electrolytic]"]
  R20 = Resistor [tolerance=±5% resistance=220k package=THT]

nets:
  GND: Q1.E, Q2.E, Q3.E, D1.anode, D2.anode, U1.Ground, C2.0, C3.0, C4.-
  N1: Q1.B, R1.Pin_1, D1.cathode
  N2: Q1.C, R2.Pin_0, R4.Pin_0
  N3: Q2.B, R2.Pin_1
  N4: Q2.C, R5.Pin_0, C1.1, U1.Reset, Release.leg1, Release.wiper
  N5: Q3.B, R3.Pin_1, D2.cathode
  N6: Q3.C, R6.Pin_0, R7.Pin_0
  gate: R1.Pin_0
  N7: R3.Pin_0, C1.0
  5V: R4.Pin_1, R5.Pin_1, R6.Pin_1, U1.Vcc_Supply_Voltage, C3.1, R11.Pin_1
  N8: R7.Pin_1, U1.Trigger
  N9: U1.Output, D3.anode
  N10: U1.Control_Voltage, C2.1
  Threshold: U1.Threshold, C4.+, U2.connector2
  Discharge: U1.Discharge, Sustain.leg1
  N11: D3.cathode, R8.Pin_0
  N12: R8.Pin_1, Attack.leg2
  N13: Attack.leg1, Attack.wiper, D4.anode, D5.anode
  N14: D4.cathode, R9.Pin_0
  N15: R9.Pin_1, Release.leg2
  N16: D5.cathode, R10.Pin_1
  N17: R10.Pin_0, Decay.leg2
  N18: U2.connector0, R13.Pin_1, IC1.pin3
  N19: U2.connector1, R12.Pin_0, R13.Pin_0
  -9V: U2.connector3, C5.1, IC1.pin4, IC2.connector5, IC2.connector15, IC2_3.pin16, Part1.pin6, C6.0, R18.Pin_0
  N20: U2.connector4, Sustain.wiper
  N21: U2.connector5, U2.connector6, Decay.leg1, Decay.wiper
  9V: U2.connector7, C5.0, IC1.pin7, R14.Pin_0, IC2.connector10, IC2_2.pin11, C6.1
  N22: R11.Pin_0, Sustain.leg2
  VGND: R12.Pin_1, R16.wiper, R19.Pin_0
  N23: IC1.pin2, R14.Pin_1, R15.Pin_1
  To Filter Amp Bias Inputs: IC1.pin6, R15.Pin_0, R20.Pin_0
  N24: IC2.connector0, IC2_1.pin1, R20.Pin_1
  N25: IC2.connector2, IC2_1.pin3, R16.leg1, R17.Pin_1
  N26: IC2.connector3, IC2_1.pin4, R16.leg2
  N27: IC2.connector4, IC2.connector6, IC2_1.pin5, IC2_2.pin7, R19.Pin_1
  N28: IC2.connector7, IC2_2.pin8, R18.Pin_1, C7.+
  From filter output: R17.Pin_0
  Audio Output: C7.-

notes:
  Terminated (unused) 1/2 LM13700

custom parts:
  OTA: Operational Transconductance Amplifier
  OTA: Operational Transconductance Amplifier
  OTA: Operational Transconductance Amplifier
  OTA: Operational Transconductance Amplifier
  OTA: Operational Transconductance Amplifier
  OTA: Operational Transconductance Amplifier
