# Fritzing sketch BITBA555_tutorial5 (saved by Fritzing 0.9.3b)
circuit board: 15cm x 10cm
breadboards: 1

parts:
  S2 = Pushbutton [package="[THT]"]
  R8 = Resistor [tolerance=±5% resistance=1k package=THT]
  C3 = Ceramic Capacitor [capacitance=100nF package="100 mil [THT, multilayer]"]
  SharpPC818 = Sharp PC817 [package=THT]
  D2 = Rectifier Diode [part_number=1N4001 package="300 mil [THT]"]
  MIDI_OUT1 = MIDI_CONN_FEMALE_SUPPORT [package=din_5_female_support]
  R9 = Resistor [tolerance=±5% resistance=180 package=THT]
  R10 = Resistor [tolerance=±5% resistance=560 package=THT]
  R11 = Resistor [tolerance=±5% resistance=220 package=THT]
  R12 = Resistor [tolerance=±5% resistance=220 package=THT]
  Arduino_Uno1 = Arduino Uno (Rev3)
  MCP4922 = IC, DIP package, 8 pins [chip_label=IC]
  C4 = Ceramic Capacitor [capacitance=100nF package="100 mil [THT, multilayer]"]
  MIDI_IN1 = MIDI_CONN_FEMALE_SUPPORT [package=din_5_female_support]
  uA742 = IC, DIP package, 8 pins [chip_label=IC]
  R13 = Resistor [tolerance=±5% resistance=220k package=THT]
  R14 = Resistor [tolerance=±5% resistance=220k package=THT]
  uA743 = IC, DIP package, 8 pins [chip_label=IC]
  R15 = Resistor [tolerance=±5% resistance=180 package=THT]
  C5 = Ceramic Capacitor [capacitance=10pF package="100 mil [THT, multilayer]"]
  C6 = Electrolytic Capacitor [capacitance=10µF voltage=20V package="100 mil [THT, electrolytic]"]
  C7 = Electrolytic Capacitor [capacitance=100µF voltage=20V package="200 mil [THT, electrolytic]"]
  IC3_2 = OTA [package="DIP (Dual Inline) [THT]"]
  IC3_3 = OTA [package="DIP (Dual Inline) [THT]"]
  IC3 = OTA [package="DIP (Dual Inline) [THT]"]
  Filter_LM13700_2 = OTA [package="DIP (Dual Inline) [THT]"]
  IC3_4 = OTA [package="DIP (Dual Inline) [THT]"]
  Part1 = OTA [package="DIP (Dual Inline) [THT]"]
  Part2 = OTA [package="DIP (Dual Inline) [THT]"]
  IC4_4 = OTA [package="DIP (Dual Inline) [THT]"]
  Filter_LM13700_1 = OTA [package="DIP (Dual Inline) [THT]"]
  IC4_2 = OTA [package="DIP (Dual Inline) [THT]"]
  Filter_LM13700_1_2 = OTA [package="DIP (Dual Inline) [THT]"]
  IC4 = OTA [package="DIP (Dual Inline) [THT]"]
  R32 = Resistor [tolerance=±5% resistance=180 package=THT]
  R33 = Resistor [tolerance=±5% resistance=180 package=THT]
  R34 = Resistor [tolerance=±5% resistance=100k package=THT]
  R35 = Resistor [tolerance=±5% resistance=100k package=THT]
  R36 = Resistor [tolerance=±5% resistance=15k package=THT]
  R37 = Resistor [tolerance=±5% resistance=15k package=THT]
  R38 = Resistor [tolerance=±5% resistance=180 package=THT]
  R39 = Resistor [tolerance=±5% resistance=180 package=THT]
  R40 = Resistor [tolerance=±5% resistance=10k package=THT]
  R41 = Resistor [tolerance=±5% resistance=10k package=THT]
  R42 = Resistor [tolerance=±5% resistance=100k package=THT]
  R43 = Resistor [tolerance=±5% resistance=100k package=THT]
  R44 = Resistor [tolerance=±5% resistance=15k package=THT]
  R45 = Resistor [tolerance=±5% resistance=15k package=THT]
  R46 = Resistor [tolerance=±5% resistance=100k package=THT]
  R47 = Resistor [tolerance=±5% resistance=100k package=THT]
  R48 = Resistor [tolerance=±5% resistance=180 package=THT]
  R49 = Resistor [tolerance=±5% resistance=180 package=THT]
  R50 = Resistor [tolerance=±5% resistance=10k package=THT]
  R51 = Resistor [tolerance=±5% resistance=10k package=THT]
  R52 = Resistor [tolerance=±5% resistance=100k package=THT]
  R53 = Resistor [tolerance=±5% resistance=100k package=THT]
  C11 = Ceramic Capacitor [capacitance=300pF package="100 mil [THT, multilayer]"]
  C12 = Ceramic Capacitor [capacitance=300pF package="100 mil [THT, multilayer]"]
  R54 = Resistor [tolerance=±5% resistance=180 package=THT]
  R55 = Resistor [tolerance=±5% resistance=180 package=THT]
  C13 = Ceramic Capacitor [capacitance=300pF package="100 mil [THT, multilayer]"]
  C14 = Ceramic Capacitor [capacitance=300pF package="100 mil [THT, multilayer]"]
  R56 = Rotary Potentiometer (Small) [maximum_resistance=1MΩ package=THT]
  R57 = Resistor [tolerance=±5% resistance=50k package=THT]
  R58 = Rotary Potentiometer (Small) [maximum_resistance=1MΩ package=THT]
  R59 = Resistor [tolerance=±5% resistance=1k package=THT]
  C15 = Ceramic Capacitor [capacitance=100nF package="100 mil [THT, multilayer]"]
  C16 = Ceramic Capacitor [capacitance=100nF package="100 mil [THT, multilayer]"]
  Attack1 = Rotary Potentiometer (Small) [maximum_resistance=1M package=THT]
  C17 = Electrolytic Capacitor [capacitance=3.3µF package="100 mil [THT, electrolytic]"]
  D6 = Rectifier Diode [part_number=1N4148 package="300 mil [THT]"]
  R60 = Resistor [tolerance=±5% resistance=180 package=THT]
  Release1 = Rotary Potentiometer (Small) [maximum_resistance=500k package=THT]
  D7 = Rectifier Diode [part_number=1N4001 package="300 mil [THT]"]
  R61 = Resistor [tolerance=±5% resistance=180 package=THT]
  U3 = LM 358 Dual Op-Amp [part_number=LM358 package="DIP8 [THT]"]
  Decay1 = Rotary Potentiometer (Small) [maximum_resistance=500k package=THT]
  R62 = Resistor [tolerance=±5% resistance=5.6k package=THT]
  Sustain1 = Rotary Potentiometer (Small) [maximum_resistance=500k package=THT]
  R63 = Resistor [tolerance=±5% resistance=5.6k package=THT]
  R64 = Resistor [tolerance=±5% resistance=10k package=THT]
  C18 = Ceramic Capacitor [capacitance=100nF package="100 mil [THT, multilayer]"]
  IC5 = IC, DIP package, 8 pins [chip_label=IC part_number=OP27]
  R65 = Resistor [tolerance=±5% resistance=10k package=THT]
  R66 = Resistor [tolerance=±5% resistance=10k package=THT]
  Q4 = NPN-Transistor [package="TO92 [THT]"]
  Q5 = NPN-Transistor [package="TO92 [THT]"]
  Q6 = NPN-Transistor [package="TO92 [THT]"]
  R67 = Resistor [tolerance=±5% resistance=5.6k package=THT]
  R68 = Resistor [tolerance=±5% resistance=5.6k package=THT]
  R69 = Resistor [tolerance=±5% resistance=5.6k package=THT]
  R70 = Resistor [tolerance=±5% resistance=10k package=THT]
  R71 = Resistor [tolerance=±5% resistance=10k package=THT]
  R72 = Resistor [tolerance=±5% resistance=10k package=THT]
  C19 = Ceramic Capacitor [capacitance=100nF package="100 mil [THT, multilayer]"]
  D8 = Rectifier Diode [part_number=1N4148 package="300 mil [THT]"]
  D9 = Rectifier Diode [part_number=1N4148 package="300 mil [THT]"]
  R73 = Resistor [tolerance=±5% resistance=1k package=THT]
  U4 = 555 Timer [part_number=NE555 package="DIP8 [THT]"]
  C20 = Ceramic Capacitor [capacitance=100nF package="100 mil [THT, multilayer]"]
  C21 = Ceramic Capacitor [capacitance=100nF package="100 mil [THT, multilayer]"]
  D10 = Rectifier Diode [part_number=1N4148 package="300 mil [THT]"]
  R74 = Resistor [tolerance=±5% resistance=180 package=THT]
  R75 = Resistor [tolerance=±5% resistance=2.2k package=THT]
  Part3 = OTA [package="DIP (Dual Inline) [THT]"]
  IC6_4 = OTA [package="DIP (Dual Inline) [THT]"]  # not connected
  IC6_3 = OTA [package="DIP (Dual Inline) [THT]"]
  IC6_2 = OTA [package="DIP (Dual Inline) [THT]"]
  IC6_1 = OTA [package="DIP (Dual Inline) [THT]"]
  IC6 = OTA [package="DIP (Dual Inline) [THT]"]
  R76 = Rotary Potentiometer (Small) [maximum_resistance=1k package=THT]
  R77 = Resistor [tolerance=±5% resistance=30k package=THT]
  C22 = Ceramic Capacitor [capacitance=100nF package="100 mil [THT, multilayer]"]
  R78 = Resistor [tolerance=±5% resistance=5.6k package=THT]
  R79 = Resistor [tolerance=±5% resistance=30k package=THT]
  C23 = Electrolytic Capacitor [capacitance=47µF package="100 mil [THT, electrolytic]"]
  R80 = Resistor [tolerance=±5% resistance=220k package=THT]

nets:
  VGND: S2.Pin_1, S2.Pin_2, C3.0, SharpPC818.Pin_3, Arduino_Uno1.GND, MCP4922.pin5, MCP4922.pin7, C4.0, uA742.pin2, uA743.pin2, uA743.pin6, C5.1, R32.Pin_1, R33.Pin_1, R38.Pin_0, R39.Pin_0, R48.Pin_1, R49.Pin_1, C11.0, C12.0, R54.Pin_0, R55.Pin_0, C17.-, R63.Pin_1, Q4.E, Q5.E, Q6.E, D8.anode, D9.anode, U4.Ground, C20.0, C21.0, R76.wiper, R79.Pin_0
  N1: S2.Pin_3, S2.Pin_4, R8.Pin_1, C3.1, Arduino_Uno1.D9_PWM
  5V: R8.Pin_0, R10.Pin_1, R11.Pin_1, Arduino_Uno1.5V, MCP4922.pin1, MCP4922.pin6, C4.1, R62.Pin_1, R70.Pin_1, R71.Pin_1, R72.Pin_1, U4.Vcc_Supply_Voltage, C21.1
  N2: SharpPC818.Pin_1, D2.cathode, R9.Pin_1
  N3: SharpPC818.Pin_2, D2.anode, MIDI_IN1.MIDI_IN
  N4: SharpPC818.Pin_4, R10.Pin_0, Arduino_Uno1.D0/RX
  N5: MIDI_OUT1.MIDI_IN, R12.Pin_0
  N6: MIDI_OUT1.MIDI_OUT, R11.Pin_0
  N7: R9.Pin_0, MIDI_IN1.MIDI_OUT
  N8: R12.Pin_1, Arduino_Uno1.D1/TX
  N9: Arduino_Uno1.D10_PWM/SS, MCP4922.pin2
  N10: Arduino_Uno1.D11_PWM/MOSI, MCP4922.pin4
  Gate: Arduino_Uno1.D12/MISO, R67.Pin_0
  N11: Arduino_Uno1.D13/SCK, MCP4922.pin3
  Osc Out: MCP4922.pin8, R35.Pin_0
  N12: uA742.pin3, R13.Pin_1, R14.Pin_0
  GND: uA742.pin4, R13.Pin_0, uA743.pin4, C6.-, C7.-, IC3.connector5, Part1.pin6, Part2.pin6, IC4.connector5, R40.Pin_0, R41.Pin_0, R50.Pin_0, R51.Pin_0, C15.0, C16.0, U3.connector3, C18.1, IC5.pin4, Part3.pin6, IC6_3.pin16, IC6.connector5, IC6.connector15, C22.0, R78.Pin_0
  N13: uA742.pin6, R15.Pin_0, C5.0
  18V: uA742.pin7, R14.Pin_1, uA743.pin7, C6.+, C7.+, IC3_2.pin11, IC3.connector10, IC4_2.pin11, IC4.connector10, R36.Pin_0, R37.Pin_0, R44.Pin_0, R45.Pin_0, C15.1, C16.1, U3.connector7, C18.0, IC5.pin7, R65.Pin_0, IC6_2.pin11, IC6.connector10, C22.1
  N14: uA743.pin3, R15.Pin_1
  N15: IC3_2.pin7, IC3.connector4, IC3.connector6, Filter_LM13700_2.pin5, C13.1
  N16: IC3_2.pin8, IC3.connector7, R40.Pin_1, R42.Pin_1, R46.Pin_0
  N17: IC3_3.pin12, IC3.connector9, IC3.connector11, IC3_4.pin10, C11.1
  N18: IC3_3.pin13, IC3.connector12, R52.Pin_1, R54.Pin_1
  N19: IC3_3.pin14, IC3.connector13, R46.Pin_1, R48.Pin_0
  N20: IC3_3.pin15, IC3.connector14, R44.Pin_1
  N21: IC3_3.pin16, IC3.connector0, IC3.connector15, Filter_LM13700_2.pin1, Filter_LM13700_1.pin16, Filter_LM13700_1_2.pin1, IC4.connector0, IC4.connector15, R59.Pin_1
  N22: IC3.connector1, Filter_LM13700_2.pin2, R36.Pin_1
  N23: IC3.connector2, Filter_LM13700_2.pin3, R32.Pin_0, R34.Pin_1
  N24: IC3.connector3, Filter_LM13700_2.pin4, R38.Pin_1, R42.Pin_0
  Filter Out: IC3.connector8, IC3_4.pin9, R50.Pin_1, R52.Pin_0, C13.0, R56.leg1, R56.wiper, R77.Pin_0
  N25: IC4_4.pin9, IC4.connector8, R34.Pin_0, R51.Pin_1, R53.Pin_0, C14.0
  N26: IC4_4.pin10, Filter_LM13700_1.pin12, IC4.connector9, IC4.connector11, C12.1
  N27: Filter_LM13700_1.pin13, IC4.connector12, R53.Pin_1, R55.Pin_1
  N28: Filter_LM13700_1.pin14, IC4.connector13, R47.Pin_1, R49.Pin_0
  N29: Filter_LM13700_1.pin15, IC4.connector14, R45.Pin_1
  N30: IC4_2.pin7, Filter_LM13700_1_2.pin5, IC4.connector4, IC4.connector6, C14.1
  N31: IC4_2.pin8, IC4.connector7, R41.Pin_1, R43.Pin_1, R47.Pin_0
  N32: Filter_LM13700_1_2.pin2, IC4.connector1, R37.Pin_1
  N33: Filter_LM13700_1_2.pin3, IC4.connector2, R33.Pin_0, R35.Pin_1
  N34: Filter_LM13700_1_2.pin4, IC4.connector3, R39.Pin_1, R43.Pin_0, R57.Pin_0
  N35: R56.leg2, R57.Pin_1
  N36: R58.leg1, R58.wiper, R59.Pin_0
  CV: R58.leg2, IC5.pin6, R66.Pin_0, R80.Pin_0
  Threshold: Attack1.leg1, Attack1.wiper, C17.+, D6.anode, D7.anode, U3.connector2, U4.Threshold
  N37: Attack1.leg2, R74.Pin_1
  N38: D6.cathode, R60.Pin_0
  N39: R60.Pin_1, Release1.leg2
  N40: Release1.leg1, Release1.wiper, Q5.C, R71.Pin_0, C19.1, U4.Reset
  N41: D7.cathode, R61.Pin_1
  N42: R61.Pin_0, Decay1.leg2
  N43: U3.connector0, R64.Pin_1, IC5.pin3
  N44: U3.connector1, R64.Pin_0, R75.Pin_0
  N45: U3.connector4, Sustain1.wiper
  N46: U3.connector5, U3.connector6, Decay1.leg1, Decay1.wiper
  N47: R62.Pin_0, Sustain1.leg2
  Discharge: Sustain1.leg1, U4.Discharge
  N48: R63.Pin_0, R75.Pin_1
  N49: IC5.pin2, R65.Pin_1, R66.Pin_1
  N50: Q4.B, R67.Pin_1, D9.cathode
  N51: Q4.C, R68.Pin_0, R70.Pin_0
  N52: Q5.B, R68.Pin_1
  N53: Q6.B, R69.Pin_1, D8.cathode
  N54: Q6.C, R72.Pin_0, R73.Pin_0
  N55: R69.Pin_0, C19.0
  N56: R73.Pin_1, U4.Trigger
  N57: U4.Output, D10.anode
  N58: U4.Control_Voltage, C20.1
  N59: D10.cathode, R74.Pin_0
  N60: IC6_2.pin7, IC6_1.pin5, IC6.connector4, IC6.connector6, R79.Pin_1
  N61: IC6_2.pin8, IC6.connector7, R78.Pin_1, C23.+
  N62: IC6_1.pin1, IC6.connector0, R80.Pin_1
  N63: IC6_1.pin3, IC6.connector2, R76.leg1, R77.Pin_1
  N64: IC6_1.pin4, IC6.connector3, R76.leg2
  Audio Output: C23.-

notes:
  Digital Oscillator Section
  Power Section
  Filter Section
  Envelope Generator Section
  Terminated (unused) 1/2 LM13700
  Amplifier Section
  Audio Out ->
  Supply1GND->
  <-Supply1_9V
  <-Supply2_18V
  Supply2_GND->
  NOTE!!! MIDI Pins 4 and 5 Flipped Because Whoever Put the MIDI Connector in the Part Library Screwed Up the Pin Numbering

custom parts:
  OTA: Operational Transconductance Amplifier
  OTA: Operational Transconductance Amplifier
  OTA: Operational Transconductance Amplifier
  OTA: Operational Transconductance Amplifier
  OTA: Operational Transconductance Amplifier
  OTA: Operational Transconductance Amplifier
